// Logisim project part1.circ as structural Verilog
module NAND (
  input  a,
  input  b,
  output out_3
);

  wire and_1_out;

  and and_1 (and_1_out, a, b);
  not not_1 (out_3, and_1_out);
endmodule

module NOR (
  input  a,
  input  b,
  output out_3
);

  wire or_1_out;

  or or_1 (or_1_out, a, b);
  not not_1 (out_3, or_1_out);
endmodule

module XOR (
  input  b,
  input  a,
  output out_3
);

  wire not_1_out;

  not not_1 (not_1_out, b);
  _2to1MUX u_2to1mux_1 (.a(b), .b(not_1_out), .s(a), .out_4(out_3));
endmodule

module _2to1MUX (
  input  a,
  input  b,
  input  s,
  output out_4
);

  wire and_1_out, and_2_out, not_1_out;

  not not_1 (not_1_out, s);
  and and_1 (and_1_out, a, not_1_out);
  and and_2 (and_2_out, s, b);
  or or_1 (out_4, and_1_out, and_2_out);
endmodule

module _4to1MUX (
  input  a,
  input  b,
  input  s0,
  input  c,
  input  d,
  input  s1,
  output out_7
);

  wire n2to1mux_1_out_4, n2to1mux_2_out_4;

  _2to1MUX u_2to1mux_1 (.a(a), .b(b), .s(s0), .out_4(n2to1mux_1_out_4));
  _2to1MUX u_2to1mux_2 (.a(c), .b(d), .s(s0), .out_4(n2to1mux_2_out_4));
  _2to1MUX u_2to1mux_3 (.a(n2to1mux_1_out_4), .b(n2to1mux_2_out_4), .s(s1), .out_4(out_7));
endmodule
